# Fritzing sketch Project 3 (saved by Fritzing 0.9.3b)
breadboards: 1

parts:
  Part1 = Arduino Uno (Rev3)
  Part2 = Thumb Joystick
  S1 = Pushbutton [package="[THT]"]
  S2 = Pushbutton [package="[THT]"]
  S3 = Pushbutton [package="[THT]"]
  S4 = Pushbutton [package="[THT]"]
  R2 = Resistor [tolerance=±5% resistance=10k package=THT]
  R3 = Resistor [tolerance=±5% resistance=10k package=THT]
  R4 = Resistor [tolerance=±5% resistance=10k package=THT]
  R5 = Resistor [tolerance=±5% resistance=10k package=THT]

nets:
  N1: Part1.A0, Part2.VERT
  N2: Part1.A1, Part2.HORZ
  N3: Part1.D0/RX, Part2.SEL
  N4: Part1.D1/TX, S4.Pin_1, S4.Pin_2, R5.Pin_0
  N5: Part1.D2, S3.Pin_1, R4.Pin_0
  N6: Part1.D3_PWM, S2.Pin_1, R3.Pin_0
  N7: Part1.D4, S1.Pin_1, R2.Pin_0
  5V: Part1.5V, Part2.VCC, S1.Pin_3, S1.Pin_4, S2.Pin_3, S3.Pin_3, S3.Pin_4, S4.Pin_3, S4.Pin_4
  GND: Part1.GND, Part2.GND, R2.Pin_1, R3.Pin_1, R4.Pin_1, R5.Pin_1
